// Logisim project Project1.circ as structural Verilog
module FullAdder (
  input  A,
  input  B,
  input  Cin,
  output Sum,
  output Cout
);

  wire and_1_out, and_2_out, xor_1_out;

  xor xor_1 (xor_1_out, A, B);
  xor xor_2 (Sum, xor_1_out, Cin);
  and and_1 (and_1_out, xor_1_out, Cin);
  and and_2 (and_2_out, A, B);
  or or_1 (Cout, and_1_out, and_2_out);
endmodule

module RippleAdder8 (
  input  [7:0] in_1
);

  wire fulladder_1_cout, fulladder_2_cout, fulladder_3_cout, fulladder_4_cout, fulladder_5_cout,
       fulladder_6_cout, fulladder_7_cout;
  wire [7:0] undriven;

  FullAdder fulladder_1 (.A(undriven[7]), .Cout(fulladder_1_cout));  // open: B, Cin, Sum
  FullAdder fulladder_2 (.A(undriven[6]), .Cin(fulladder_1_cout), .Cout(fulladder_2_cout));  // open: B, Sum
  FullAdder fulladder_3 (.A(undriven[5]), .Cin(fulladder_2_cout), .Cout(fulladder_3_cout));  // open: B, Sum
  FullAdder fulladder_4 (.A(undriven[4]), .Cin(fulladder_3_cout), .Cout(fulladder_4_cout));  // open: B, Sum
  FullAdder fulladder_5 (.A(undriven[3]), .Cin(fulladder_4_cout), .Cout(fulladder_5_cout));  // open: B, Sum
  FullAdder fulladder_6 (.A(undriven[2]), .Cin(fulladder_5_cout), .Cout(fulladder_6_cout));  // open: B, Sum
  FullAdder fulladder_7 (.A(undriven[1]), .Cin(fulladder_6_cout), .Cout(fulladder_7_cout));  // open: B, Sum
  FullAdder fulladder_8 (.A(undriven[0]), .Cin(fulladder_7_cout));  // open: B, Sum, Cout
endmodule
